// Digital circuit overture.dig as structural Verilog
module overture (
);

  wire and_2_out, and_3_out, and_4_out, and_5_out, and_6_out, and_7_out, and_8_out, and_9_out, and_10_out,
       and_11_out, and_12_out, and_13_out, and_14_out, and_15_out, and_16_out, and_17_out, and_18_out,
       and_19_out, and_20_out, and_21_out, and_22_out, and_23_out, and_24_out, and_25_out, and_26_out,
       and_27_out, and_28_out, and_29_out, and_30_out, and_31_out, and_32_out, and_33_out, and_34_out,
       and_35_out, and_36_out, and_37_out, and_38_out, and_39_out, and_40_out, and_41_out, and_42_out,
       and_43_out, and_44_out, and_45_out, and_46_out, and_47_out, and_48_out, and_49_out, and_50_out,
       and_51_out, and_52_out, dipswitch_1_out, dipswitch_2_out, dipswitch_3_out, nand_1_out, nand_2_out,
       nand_3_out, nand_4_out, nand_5_out, nand_6_out, nand_7_out, nand_8_out, nor_1_out, nor_2_out,
       nor_3_out, nor_4_out, nor_5_out, nor_6_out, nor_7_out, nor_8_out, nor_9_out, nor_10_out, nor_11_out,
       nor_12_out, nor_13_out, nor_14_out, nor_15_out, nor_16_out, nor_17_out, nor_18_out, nor_19_out,
       nor_20_out, nor_21_out, nor_22_out, nor_23_out, nor_24_out, nor_25_out, nor_26_out, not_1_out,
       not_2_out, not_3_out, not_4_out, not_5_out, not_6_out, not_7_out, not_8_out, not_9_out, or_1_out,
       or_2_out, or_3_out, or_4_out, or_5_out, or_6_out, or_7_out, or_8_out, or_9_out, or_10_out, or_11_out,
       or_12_out, or_13_out, or_14_out, or_15_out, or_16_out, undriven, undriven_2, undriven_3, undriven_4,
       undriven_5, undriven_6, undriven_7, undriven_8, undriven_9, undriven_10, undriven_11, undriven_12,
       undriven_13, undriven_14, undriven_15, undriven_16, undriven_17, undriven_18, undriven_19,
       undriven_20, undriven_21, undriven_22, undriven_23, undriven_24, undriven_25, undriven_26,
       undriven_27, undriven_28, undriven_29, undriven_30, undriven_31, undriven_32, undriven_33,
       undriven_34, undriven_35, undriven_36, undriven_37, undriven_38, undriven_39, undriven_40,
       undriven_41, undriven_42, undriven_43, undriven_44, undriven_45, undriven_46, undriven_47,
       undriven_48, undriven_49, undriven_50, undriven_51, undriven_52, undriven_53, undriven_54,
       undriven_55, undriven_56, undriven_57, undriven_58, undriven_59, undriven_60, undriven_61,
       undriven_62, undriven_63, undriven_64, undriven_65, undriven_66, undriven_67, undriven_68,
       undriven_69, undriven_70, undriven_71, undriven_72, undriven_73, undriven_74, undriven_75,
       undriven_76, undriven_77, undriven_78, undriven_79, undriven_80, undriven_81, undriven_82,
       undriven_83, undriven_84, undriven_85, undriven_86, undriven_87, undriven_88, undriven_89,
       undriven_90, undriven_91, xor_1_out, xor_2_out, xor_3_out, xor_4_out, xor_5_out, xor_6_out, xor_7_out,
       xor_8_out, xor_9_out, xor_10_out, xor_11_out, xor_12_out, xor_13_out, xor_14_out, xor_15_out,
       xor_16_out;

  // And and_1 is placed but not wired
  DipSwitch dipswitch_1 (.out(dipswitch_1_out));
  DipSwitch dipswitch_2 (.out(dipswitch_2_out));
  DipSwitch dipswitch_3 (.out(dipswitch_3_out));
  not not_1 (not_1_out, undriven);
  and and_2 (and_2_out, undriven_9, undriven);
  not not_2 (not_2_out, undriven_2);
  and and_3 (and_3_out, undriven_9, undriven_2);
  not not_3 (not_3_out, undriven_3);
  and and_4 (and_4_out, undriven_9, undriven_3);
  not not_4 (not_4_out, undriven_4);
  and and_5 (and_5_out, undriven_9, undriven_4);
  not not_5 (not_5_out, undriven_5);
  and and_6 (and_6_out, undriven_9, undriven_5);
  not not_6 (not_6_out, undriven_6);
  and and_7 (and_7_out, undriven_9, undriven_6);
  not not_7 (not_7_out, undriven_7);
  and and_8 (and_8_out, undriven_9, undriven_7);
  not not_8 (not_8_out, undriven_8);
  and and_9 (and_9_out, undriven_9, undriven_8);
  and and_10 (and_10_out, not_9_out, dipswitch_2_out);
  not not_9 (not_9_out, dipswitch_3_out);
  and and_11 (and_11_out, dipswitch_2_out, dipswitch_3_out);
  and and_12 (and_12_out, not_1_out, undriven_9);
  and and_13 (and_13_out, not_2_out, undriven_9);
  and and_14 (and_14_out, not_3_out, undriven_9);
  and and_15 (and_15_out, not_4_out, undriven_9);
  and and_16 (and_16_out, not_5_out, undriven_9);
  and and_17 (and_17_out, not_6_out, undriven_9);
  and and_18 (and_18_out, not_7_out, undriven_9);
  and and_19 (and_19_out, not_8_out, undriven_9);
  nor nor_1 (nor_1_out, and_12_out, nor_2_out);
  nor nor_2 (nor_2_out, nor_1_out, and_2_out);
  nor nor_3 (nor_3_out, and_13_out, nor_4_out);
  nor nor_4 (nor_4_out, nor_3_out, and_3_out);
  nor nor_5 (nor_5_out, and_14_out, nor_6_out);
  nor nor_6 (nor_6_out, nor_5_out, and_4_out);
  nor nor_7 (nor_7_out, and_15_out, nor_8_out);
  nor nor_8 (nor_8_out, nor_7_out, and_5_out);
  nor nor_9 (nor_9_out, and_16_out, nor_10_out);
  nor nor_10 (nor_10_out, nor_9_out, and_6_out);
  nor nor_11 (nor_11_out, and_17_out, nor_12_out);
  nor nor_12 (nor_12_out, nor_11_out, and_7_out);
  nor nor_13 (nor_13_out, and_18_out, nor_14_out);
  nor nor_14 (nor_14_out, nor_13_out, and_8_out);
  nor nor_15 (nor_15_out, and_19_out, nor_16_out);
  nor nor_16 (nor_16_out, nor_15_out, and_9_out);
  and and_20 (and_20_out, undriven_10, undriven_14);
  xor xor_1 (xor_1_out, undriven_14, undriven_10);
  and and_21 (and_21_out, undriven_11, undriven_15);
  xor xor_2 (xor_2_out, undriven_15, undriven_11);
  and and_22 (and_22_out, undriven_12, undriven_16);
  xor xor_3 (xor_3_out, undriven_16, undriven_12);
  and and_23 (and_23_out, undriven_13, undriven_17);
  xor xor_4 (xor_4_out, undriven_17, undriven_13);
  and and_24 (and_24_out, undriven_18, undriven_20);
  xor xor_5 (xor_5_out, undriven_20, undriven_18);
  and and_25 (and_25_out, undriven_19, undriven_21);
  xor xor_6 (xor_6_out, undriven_21, undriven_19);
  and and_26 (and_26_out, undriven_90, undriven_22);
  xor xor_7 (xor_7_out, undriven_22, undriven_90);
  and and_27 (and_27_out, undriven_91, undriven_23);
  xor xor_8 (xor_8_out, undriven_23, undriven_91);
  nor nor_17 (nor_17_out, and_10_out, nor_18_out);
  nor nor_18 (nor_18_out, nor_17_out, and_11_out);
  or or_1 (or_1_out, and_20_out, and_28_out);
  and and_28 (and_28_out, xor_1_out, or_2_out);
  xor xor_9 (xor_9_out, xor_1_out, or_2_out);
  or or_2 (or_2_out, and_21_out, and_29_out);
  and and_29 (and_29_out, xor_2_out, or_3_out);
  xor xor_10 (xor_10_out, xor_2_out, or_3_out);
  or or_3 (or_3_out, and_22_out, and_30_out);
  and and_30 (and_30_out, xor_3_out, or_4_out);
  xor xor_11 (xor_11_out, xor_3_out, or_4_out);
  or or_4 (or_4_out, and_23_out, and_31_out);
  and and_31 (and_31_out, xor_4_out, or_5_out);
  xor xor_12 (xor_12_out, xor_4_out, or_5_out);
  or or_5 (or_5_out, and_24_out, and_40_out);
  or or_6 (or_6_out, and_25_out, and_41_out);
  or or_7 (or_7_out, and_26_out, and_42_out);
  or or_8 (or_8_out, and_27_out, and_43_out);
  Reset reset_1 ();  // open: out
  Reset reset_2 ();  // open: out
  and and_32 (and_32_out, nor_1_out, undriven_24);
  Reset reset_3 ();  // open: out
  and and_33 (and_33_out, nor_3_out, undriven_24);
  Reset reset_4 ();  // open: out
  and and_34 (and_34_out, nor_5_out, undriven_24);
  Reset reset_5 ();  // open: out
  and and_35 (and_35_out, nor_7_out, undriven_24);
  Reset reset_6 ();  // open: out
  and and_36 (and_36_out, nor_9_out, undriven_24);
  Reset reset_7 ();  // open: out
  and and_37 (and_37_out, nor_11_out, undriven_24);
  Reset reset_8 ();  // open: out
  and and_38 (and_38_out, nor_13_out, undriven_24);
  Reset reset_9 ();  // open: out
  and and_39 (and_39_out, nor_15_out, undriven_24);
  and and_40 (and_40_out, xor_5_out, or_6_out);
  xor xor_13 (xor_13_out, xor_5_out, or_6_out);
  and and_41 (and_41_out, xor_6_out, or_7_out);
  xor xor_14 (xor_14_out, xor_6_out, or_7_out);
  and and_42 (and_42_out, xor_7_out, or_8_out);
  xor xor_15 (xor_15_out, xor_7_out, or_8_out);
  and and_43 (and_43_out, xor_8_out, undriven_25);
  xor xor_16 (xor_16_out, xor_8_out, undriven_25);
  and and_44 (and_44_out, nor_17_out, dipswitch_1_out);
  and and_45 (and_45_out, undriven_32, undriven_40);
  or or_9 (or_9_out, undriven_48, undriven_56);
  and and_46 (and_46_out, undriven_31, undriven_39);
  or or_10 (or_10_out, undriven_47, undriven_55);
  and and_47 (and_47_out, undriven_30, undriven_38);
  and and_48 (and_48_out, undriven_29, undriven_37);
  or or_11 (or_11_out, undriven_46, undriven_54);
  or or_12 (or_12_out, undriven_45, undriven_53);
  and and_49 (and_49_out, undriven_28, undriven_36);
  or or_13 (or_13_out, undriven_44, undriven_52);
  and and_50 (and_50_out, undriven_27, undriven_35);
  or or_14 (or_14_out, undriven_43, undriven_51);
  and and_51 (and_51_out, undriven_26, undriven_34);
  and and_52 (and_52_out, undriven_57, undriven_33);
  or or_15 (or_15_out, undriven_42, undriven_50);
  or or_16 (or_16_out, undriven_41, undriven_49);
  nand nand_1 (nand_1_out, undriven_64, undriven_72);
  nor nor_19 (nor_19_out, undriven_80, undriven_88);
  nand nand_2 (nand_2_out, undriven_63, undriven_71);
  nand nand_3 (nand_3_out, undriven_62, undriven_70);
  nor nor_20 (nor_20_out, undriven_79, undriven_87);
  nor nor_21 (nor_21_out, undriven_78, undriven_86);
  nand nand_4 (nand_4_out, undriven_61, undriven_69);
  nor nor_22 (nor_22_out, undriven_77, undriven_85);
  nand nand_5 (nand_5_out, undriven_60, undriven_68);
  nor nor_23 (nor_23_out, undriven_76, undriven_84);
  nand nand_6 (nand_6_out, undriven_59, undriven_67);
  nand nand_7 (nand_7_out, undriven_58, undriven_66);
  nor nor_24 (nor_24_out, undriven_75, undriven_83);
  nor nor_25 (nor_25_out, undriven_74, undriven_82);
  nand nand_8 (nand_8_out, undriven_89, undriven_65);
  nor nor_26 (nor_26_out, undriven_73, undriven_81);

  // Notes on the sheet:
  //   Register
  //   Save
  //   Load
  //   Save Value
  //   ADDER
  //   1 Bit mem
  //   SaveVal
  //   .
  //   Reset
  //   Write
  //   Always OUT
  //   OUT
  //   Always On Out
  //   Out
  //   AND
  //   OR
  //   NAND
  //   NOR
endmodule
